# Fritzing sketch Untitled Sketch 2 (saved by Fritzing 0.9.3b)

parts:
  U1 = NodeMCU V1.0
  Part1 = SRF05 Ultrasonic Rangefinder
  J1 = Piezo Speaker

nets:
  N1: U1.D3, J1.pin2
  3V3: U1.3V3, Part1.VCC
  N2: U1.D6, Part1.Trig
  N3: U1.D7, Part1.Echo

custom parts:
  NodeMCU V1.0: ESP8266 based NodeMCU
